# Fritzing sketch schematicBluetooth (saved by Fritzing 0.9.3b)
breadboards: 1

parts:
  R1 = Resistor [tolerance=±5% resistance=220 package="1206 [SMD]"]
  R2 = Resistor [tolerance=±5% resistance=220 package="1206 [SMD]"]
  S1 = Pushbutton [package="[SMD]"]
  S2 = Pushbutton [package="[SMD]"]
  Part1 = Bluetooth HC-05 Macho  # not connected
  Part2 = Arduino Uno (Rev3)

nets:
  N1: R1.Pin_0, S2.Pin_1, S2.Pin_2, Part2.D3_PWM
  N2: R1.Pin_1, R2.Pin_1, Part2.GND
  N3: R2.Pin_0, S1.Pin_1, S1.Pin_2, Part2.D2
  N4: S1.Pin_3, S1.Pin_4, S2.Pin_3, S2.Pin_4, Part2.5V
