# Fritzing sketch schematicButton (saved by Fritzing 0.9.3b)
breadboards: 1

parts:
  S1 = Pushbutton [package="[SMD]"]
  S2 = Pushbutton [package="[SMD]"]
  Part1 = Adafruit Bluefruit LE Micro [part_number="Adafruit #2661"]
  R2 = Resistor [tolerance=±5% resistance=10k package="2010 [SMD]"]
  R3 = Resistor [tolerance=±5% resistance=10k package="2010 [SMD]"]

nets:
  N1: S1.Pin_1, S1.Pin_2, Part1.13, R2.Pin_0
  N2: S1.Pin_3, S1.Pin_4, S2.Pin_3, S2.Pin_4, Part1.+3V3
  N3: S2.Pin_1, S2.Pin_2, R3.Pin_0
  N4: Part1.GND, R2.Pin_1, R3.Pin_1

custom parts:
  Adafruit Bluefruit LE Micro: Would you like to add powerful and easy-to-use Bluetooth Low Energy to your robot, art or other electronics project? Heck yeah! With BLE now included in modern smart phones and tablets, its fun to add wireless connectivity. So what you really need is the new Adafruit Bluefruit LE Micro - it's an Atmega32u4 chip (same as used as in the Adafruit Flora or Arduino Leonardo) plus our SPI Bluefruit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
